// Logisim project 6502_k.circ as structural Verilog: 10 circuits, main circuit cpu
module cpu (
  input  R,
  output CO2,
  output CO1
);

  wire alu_1_co, clock_1_out, fsm_1_aco, fsm_1_alu, fsm_1_inc, fsm_1_mlo, fsm_1_wa, fsm_1_wl, fsm_1_wo,
       fsm_1_wx, fsm_1_wy;
  wire [1:0] fsm_1_adr, fsm_1_lco, fsm_1_rx;
  wire [5:0] fsm_1_aop;
  wire [7:0] A_q, adder_1_out, alu_1_f, L_q, Mem_dout, multiplexer_3_out, multiplexer_4_out,
       multiplexer_6_out, O_q, OP, X_q, Y_q;
  wire [15:0] multiplexer_1_out, pc_1_pc, PR_q;
  wire [15:8] multiplexer_5_out;

  Clock clock_1 (.out(clock_1_out));
  Register #(.width(16)) PR (.D(multiplexer_1_out), .en(1'b1), .clk(clock_1_out), .Q(PR_q), .clr(R));
  pc pc_1 (
    .LO({8{1'b0}}), .CI(1'b0), .HI({8{1'b0}}), .WR(1'b0), .INC(fsm_1_inc), .CLK(clock_1_out), .R(R),
    .PC(pc_1_pc), .CO(CO1));
  Multiplexer #(.select(2), .width(16), .enable("false")) multiplexer_1 (
    .in0(pc_1_pc), .in1({multiplexer_5_out, multiplexer_6_out}), .in2(pc_1_pc), .in3(PR_q),
    .out(multiplexer_1_out), .sel(fsm_1_adr));
  // Probe on OP
  // Probe on multiplexer_1_out
  RAM #(.addrWidth(16), .databus("bibus")) Mem (
    .addr(multiplexer_1_out), .we(1'b0), .oe(1'b1), .clk(clock_1_out), .din({8{1'b0}}), .dout(Mem_dout));
  fsm fsm_1 (
    .GR(OP[1:0]), .XY(OP[2]), .AB(OP[3]), .ID(OP[4]), .OPC(OP[7:5]), .ACI(alu_1_co), .CLK(clock_1_out),
    .R(R), .INC(fsm_1_inc), .PRV(fsm_1_adr[1]), .ADR(fsm_1_adr[0]), .ALU(fsm_1_alu), .LCO(fsm_1_lco[0]),
    .MHI(fsm_1_lco[1]), .wO(fsm_1_wo), .wL(fsm_1_wl), .wX(fsm_1_wx), .wY(fsm_1_wy), .wA(fsm_1_wa),
    .rX(fsm_1_rx[0]), .rY(fsm_1_rx[1]), .MLO(fsm_1_mlo), .ACO(fsm_1_aco), .AOP(fsm_1_aop));
  Multiplexer #(.width(8), .enable("false")) multiplexer_2 (
    .in0(O_q), .in1(multiplexer_3_out), .out(OP), .sel(fsm_1_wo));
  Multiplexer #(.width(8), .enable("false")) multiplexer_3 (
    .in0(Mem_dout), .in1(alu_1_f), .out(multiplexer_3_out), .sel(fsm_1_alu));
  // Probe on multiplexer_3_out
  Register O (.D(multiplexer_3_out), .en(fsm_1_wo), .clk(clock_1_out), .Q(O_q), .clr(R));
  Register L (.D(multiplexer_3_out), .en(fsm_1_wl), .clk(clock_1_out), .Q(L_q), .clr(R));
  Register X (.D(multiplexer_3_out), .en(fsm_1_wx), .clk(clock_1_out), .Q(X_q), .clr(R));
  Register Y (.D(multiplexer_3_out), .en(fsm_1_wy), .clk(clock_1_out), .Q(Y_q), .clr(R));
  Register A (.D(multiplexer_3_out), .en(fsm_1_wa), .clk(clock_1_out), .Q(A_q), .clr(R));
  Adder adder_1 (.a({8{1'b0}}), .b(multiplexer_3_out), .out(adder_1_out), .cin(fsm_1_lco[0]), .cout(CO2));
  Multiplexer #(.select(2), .width(8), .enable("false")) multiplexer_4 (
    .in0(8'h1), .in1(X_q), .in2(Y_q), .in3(A_q), .out(multiplexer_4_out), .sel(fsm_1_rx));
  // Probe on L_q
  // Probe on multiplexer_4_out
  // Probe on fsm_1_aop
  Multiplexer #(.select(2), .width(8), .enable("false")) multiplexer_5 (
    .in0({8{1'b0}}), .in1(adder_1_out), .in2(multiplexer_3_out), .in3(adder_1_out), .out(multiplexer_5_out),
    .sel(fsm_1_lco));
  // Probe on multiplexer_5_out
  // Probe on multiplexer_6_out
  Multiplexer #(.width(8), .enable("false")) multiplexer_6 (
    .in0(alu_1_f), .in1(multiplexer_3_out), .out(multiplexer_6_out), .sel(fsm_1_mlo));
  alu8 alu_1 (.B(L_q), .A(multiplexer_4_out), .CI(fsm_1_aco), .OP(fsm_1_aop), .F(alu_1_f), .CO(alu_1_co));
  // Probe on alu_1_f
endmodule

module pc (
  input  [7:0] LO,
  input  CI,
  input  [7:0] HI,
  input  WR,
  input  INC,
  input  CLK,
  input  R,
  output [15:0] PC,
  output CO
);

  wire adder_1_cout, and_1_out, and_2_out, and_3_out, and_4_out, multiplexer_2_out, not_1_out, not_2_out,
       not_3_out, or_1_out, or_2_out, or_3_out;
  wire [7:0] adder_1_out, multiplexer_1_out, multiplexer_3_out, multiplexer_4_out;

  Multiplexer #(.width(8), .enable("false")) multiplexer_1 (
    .in0(adder_1_out), .in1(LO), .out(multiplexer_1_out), .sel(WR));
  and and_1 (and_1_out, or_1_out, and_3_out);
  Multiplexer #(.enable("false")) multiplexer_2 (.in0(and_4_out), .in1(CI), .out(multiplexer_2_out), .sel(WR));
  Multiplexer #(.width(8), .enable("false")) multiplexer_3 (
    .in0(adder_1_out), .in1(HI), .out(multiplexer_3_out), .sel(WR));
  or or_1 (or_1_out, WR, INC);
  not not_1 (not_1_out, and_3_out);
  Register L (.D(multiplexer_1_out), .en(or_2_out), .clk(CLK), .Q(PC[7:0]), .clr(R));
  or or_2 (or_2_out, and_1_out, WR);
  Register #(.width(1)) C (.D(and_2_out), .en(1'b1), .clk(CLK), .Q(CO), .clr(R));
  and and_2 (and_2_out, multiplexer_2_out, or_1_out);
  Register H (.D(multiplexer_3_out), .en(or_3_out), .clk(CLK), .Q(PC[15:8]), .clr(R));
  or or_3 (or_3_out, not_1_out, WR);
  not not_2 (not_2_out, WR);
  Multiplexer #(.width(8), .enable("false")) multiplexer_4 (
    .in0(PC[15:8]), .in1(PC[7:0]), .out(multiplexer_4_out), .sel(and_3_out));
  // Probe on multiplexer_4_out
  and and_3 (and_3_out, not_2_out, not_3_out);
  Adder adder_1 (.a(multiplexer_4_out), .b(8'h1), .out(adder_1_out), .cout(adder_1_cout));  // open: cin
  and and_4 (and_4_out, adder_1_cout, not_3_out);
  not not_3 (not_3_out, CO);
endmodule

module fsm (
  input  [1:0] GR,
  input  XY,
  input  AB,
  input  ID,
  input  [2:0] OPC,
  input  ACI,
  input  CLK,
  input  R,
  output INC,
  output PRV,
  output ADR,
  output ALU,
  output LCO,
  output MHI,
  output wO,
  output wL,
  output wX,
  output wY,
  output wA,
  output rX,
  output rY,
  output MLO,
  output ACO,
  output [5:0] AOP
);

  wire fsm_next_1_s0, fsm_next_1_sco, fsm_next_1_shi, fsm_next_1_sin, fsm_next_1_slo, fsm_next_1_slr,
       fsm_next_1_sop, fsm_next_sig_1_ci, fsm_next_sig_1_imm, fsm_next_sig_1_ld, fsm_next_sig_1_zp,
       fsm_next_sig_1_zpy;

  fsm_next_sig fsm_next_sig_1 (
    .GR(GR), .XY(XY), .AB(AB), .ID(ID), .OPC(OPC), .ACI(ACI), .CI(fsm_next_sig_1_ci), .ZP(fsm_next_sig_1_zp),
    .ZPY(fsm_next_sig_1_zpy), .IMM(fsm_next_sig_1_imm), .LD(fsm_next_sig_1_ld));  // open: ACC, ALU, W
  fsm_next fsm_next_1 (
    .CI(fsm_next_sig_1_ci), .ZP(fsm_next_sig_1_zp), .ZPY(fsm_next_sig_1_zpy), .IMM(fsm_next_sig_1_imm),
    .CLK(CLK), .R(R), .S0(fsm_next_1_s0), .SOP(fsm_next_1_sop), .SLO(fsm_next_1_slo), .SIN(fsm_next_1_sin),
    .SHI(fsm_next_1_shi), .SCO(fsm_next_1_sco), .SLR(fsm_next_1_slr));
  fsm_out fsm_out_1 (
    .S0(fsm_next_1_s0), .SOP(fsm_next_1_sop), .SLO(fsm_next_1_slo), .SIN(fsm_next_1_sin),
    .SHI(fsm_next_1_shi), .SCO(fsm_next_1_sco), .SLR(fsm_next_1_slr), .GR(GR), .XY(XY), .AB(AB), .ID(ID),
    .OPC(OPC), .CI(fsm_next_sig_1_ci), .ZP(fsm_next_sig_1_zp), .ZPY(fsm_next_sig_1_zpy),
    .LD(fsm_next_sig_1_ld), .INC(INC), .PRV(PRV), .ADR(ADR), .ALU(ALU), .LCO(LCO), .MHI(MHI), .wO(wO),
    .wL(wL), .wX(wX), .wY(wY), .wA(wA), .rX(rX), .rY(rY), .MLO(MLO), .ACO(ACO), .AOP(AOP));
endmodule

module fsm_next_sig (
  input  [1:0] GR,
  input  XY,
  input  AB,
  input  ID,
  input  [2:0] OPC,
  input  ACI,
  output CI,
  output ZP,
  output ZPY,
  output IMM,
  output ACC,
  output LD,
  output ALU,
  output W
);

  wire and_1_out, and_2_out, CP_out, LS_out, not_2_out, not_4_out, not_5_out, not_6_out, not_7_out,
       not_8_out, or_1_out, S_out, xor_1_out;
  wire [1:0] not_1_out;
  wire [2:0] not_3_out;

  assign not_1_out = ~GR;  // NOT_Gate not_1, 2 bits wide
  and and_1 (and_1_out, not_1_out[1], GR[0]);
  and and_2 (and_2_out, not_1_out[0], GR[1]);
  not not_2 (not_2_out, XY);
  assign not_3_out = ~OPC;  // NOT_Gate not_3, 3 bits wide
  not not_4 (not_4_out, AB);
  not not_5 (not_5_out, ID);
  xor xor_1 (xor_1_out, not_4_out, and_1_out);
  and LS (LS_out, OPC[2], not_3_out[1]);
  and CP (CP_out, OPC[1], OPC[2], not_3_out[0], and_1_out);
  and L (LD, OPC[0], LS_out);
  and S (S_out, LS_out, not_3_out[0]);
  or or_1 (or_1_out, ZPY, AB);
  not not_6 (not_6_out, LD);
  not not_7 (not_7_out, S_out);
  not not_8 (not_8_out, CP_out);
  and and_3 (CI, or_1_out, ACI);
  and and_4 (ZP, not_5_out, not_4_out, XY);
  and and_5 (ZPY, ID, not_4_out, not_2_out);
  and and_6 (IMM, not_5_out, not_2_out, xor_1_out);
  and and_7 (ACC, not_5_out, AB, not_2_out, and_2_out);
  and and_8 (ALU, not_6_out, not_7_out);
  and and_9 (W, not_6_out, not_8_out);
endmodule

module fsm_next (
  input  CI,
  input  ZP,
  input  ZPY,
  input  IMM,
  input  CLK,
  input  R,
  output S0,
  output SOP,
  output SLO,
  output SIN,
  output SHI,
  output SCO,
  output SLR
);

  wire and_3_out, and_5_out, and_6_out, and_7_out, not_1_out, not_2_out, not_3_out, not_4_out, not_5_out,
       not_6_out, not_7_out, not_8_out, not_9_out, not_10_out;
  wire [5:0] or_3_out;

  not not_1 (not_1_out, IMM);
  not not_2 (not_2_out, ZPY);
  not not_3 (not_3_out, ZP);
  not not_4 (not_4_out, CI);
  and and_1 (or_3_out[1], SOP, not_1_out);
  and and_2 (or_3_out[2], SLO, ZPY);
  and and_3 (and_3_out, SLO, not_2_out, not_3_out);
  and and_4 (or_3_out[4], SHI, CI);
  and and_5 (and_5_out, SHI, not_4_out);
  and and_6 (and_6_out, SLO, ZP);
  and and_7 (and_7_out, SOP, IMM);
  or or_1 (or_3_out[3], SIN, and_3_out);
  or or_2 (or_3_out[5], SCO, and_5_out, and_6_out, and_7_out);
  and and_8 (S0, not_5_out, not_6_out, not_7_out, not_8_out, not_9_out, not_10_out);
  or or_3 (or_3_out[0], S0, SLR);
  Register #(.width(6)) register_1 (.D(or_3_out), .en(1'b1), .clk(CLK), .Q({SLR, SCO, SHI, SIN, SLO, SOP}), .clr(R));
  not not_5 (not_5_out, SOP);
  not not_6 (not_6_out, SLO);
  not not_7 (not_7_out, SIN);
  not not_8 (not_8_out, SHI);
  not not_9 (not_9_out, SCO);
  not not_10 (not_10_out, SLR);
endmodule

module fsm_out (
  input  S0,
  input  SOP,
  input  SLO,
  input  SIN,
  input  SHI,
  input  SCO,
  input  SLR,
  input  [1:0] GR,
  input  XY,
  input  AB,
  input  ID,
  input  [2:0] OPC,
  input  CI,
  input  ZP,
  input  ZPY,
  input  LD,
  output INC,
  output PRV,
  output ADR,
  output ALU,
  output LCO,
  output MHI,
  output wO,
  output wL,
  output wX,
  output wY,
  output wA,
  output rX,
  output rY,
  output MLO,
  output ACO,
  output [5:0] AOP
);

  wire and_1_out, and_2_out, and_4_out, and_5_out, not_2_out, not_3_out, not_4_out, or_1_out, or_2_out,
       or_3_out, or_4_out;
  wire [1:0] not_1_out;

  assign not_1_out = ~GR;  // NOT_Gate not_1, 2 bits wide
  and and_1 (and_1_out, SLO, ZPY);
  or or_1 (or_1_out, ZP, ZPY);
  or or_2 (or_2_out, SHI, SCO);
  not not_2 (not_2_out, ID);
  and and_2 (and_2_out, SLR, LD);
  and and_3 (MLO, SLO, or_1_out);
  and and_4 (and_4_out, or_2_out, not_2_out);
  and and_5 (and_5_out, SHI, AB);
  and and_6 (PRV, CI, SHI);
  or or_3 (or_3_out, AB, ZPY);
  buf or_4 (or_4_out, and_2_out);  // OR_Gate
  not not_3 (not_3_out, SIN);
  not not_4 (not_4_out, XY);
  or or_5 (INC, S0, and_5_out, SOP, SLR);
  or or_6 (ADR, SHI, SIN, MLO, SCO);
  and and_7 (MHI, SHI, or_3_out);
  or or_7 (wL, SIN, SLO);
  and and_8 (wX, or_4_out, not_1_out[0], GR[1]);
  and and_9 (wY, not_1_out[0], not_1_out[1], or_4_out);
  and and_10 (wA, or_4_out, not_1_out[1], GR[0]);
  and and_11 (rX, XY, not_3_out);
  and and_12 (rY, not_3_out, not_4_out);
  Multiplexer #(.width(6), .enable("false")) multiplexer_1 (
    .in0(6'b011001), .in1(6'b000101), .out(AOP), .sel(and_4_out));

  assign ACO = 1'b0;
  assign ALU = 1'b0;
  assign LCO = SCO;
  assign wO = SOP;
endmodule

module alu8 (
  input  [7:0] B,
  input  [7:0] A,
  input  CI,
  input  [5:0] OP,
  output [7:0] F,
  output CO
);

  wire and_1_out, hi_co, lo_g, lo_p, or_1_out;
  wire [3:0] hi_f, lo_f;

  // Probe on OP
  or or_1 (or_1_out, lo_g, and_1_out);
  and and_1 (and_1_out, lo_p, CI);
  alu4 lo (.B(B[3:0]), .A(A[3:0]), .CI(CI), .S(OP[3:0]), .M(OP[4]), .G(lo_g), .P(lo_p), .F(lo_f));  // open: CO
  alu4 hi (.B(B[7:4]), .A(A[7:4]), .CI(or_1_out), .S(OP[3:0]), .M(OP[4]), .CO(hi_co), .F(hi_f));  // open: G, P
  Multiplexer #(.width(8), .enable("false")) multiplexer_1 (
    .in0({hi_f, lo_f}), .in1({CI, A[7:1]}), .out(F), .sel(OP[5]));
  Multiplexer #(.enable("false")) multiplexer_2 (.in0(hi_co), .in1(A[0]), .out(CO), .sel(OP[5]));

  // Notes on the sheet:
  //   s,m,s3-s0
endmodule

module alu4 (
  input  [3:0] B,
  input  [3:0] A,
  input  CI,
  input  [3:0] S,
  input  M,
  output CO,
  output G,
  output P,
  output [3:0] F
);

  wire and_1_out, and_2_out, and_3_out, and_4_out, and_6_out, and_7_out, and_8_out, and_9_out, and_10_out,
       and_11_out, and_12_out, and_13_out, and_14_out, and_15_out, or_2_out, or_3_out, or_4_out, pg_0_g,
       pg_0_p, pg_1_g, pg_1_p, pg_2_g, pg_2_p, pg_3_g, pg_3_p, xor_1_out, xor_2_out, xor_3_out, xor_4_out;

  pg pg_3 (.A(A[3]), .B(B[3]), .S(S), .G(pg_3_g), .P(pg_3_p));
  pg pg_2 (.A(A[2]), .B(B[2]), .S(S), .G(pg_2_g), .P(pg_2_p));
  pg pg_1 (.A(A[1]), .B(B[1]), .S(S), .G(pg_1_g), .P(pg_1_p));
  pg pg_0 (.A(A[0]), .B(B[0]), .S(S), .G(pg_0_g), .P(pg_0_p));
  and and_1 (and_1_out, CI, pg_0_p, pg_1_p, pg_2_p, pg_3_p);
  and and_2 (and_2_out, pg_0_g, pg_1_p, pg_2_p, pg_3_p);
  and and_3 (and_3_out, pg_1_g, pg_2_p, pg_3_p);
  and and_4 (and_4_out, pg_2_g, pg_3_p);
  and and_5 (P, pg_0_p, pg_1_p, pg_2_p, pg_3_p);
  and and_6 (and_6_out, M, CI, pg_0_p, pg_1_p, pg_2_p);
  and and_7 (and_7_out, M, pg_0_g, pg_1_p, pg_2_p);
  and and_8 (and_8_out, M, pg_1_g, pg_2_p);
  and and_9 (and_9_out, M, pg_2_g);
  and and_10 (and_10_out, M, CI, pg_1_p, pg_0_p);
  and and_11 (and_11_out, M, pg_0_g, pg_1_p);
  and and_12 (and_12_out, M, pg_1_g);
  and and_13 (and_13_out, M, CI, pg_0_p);
  and and_14 (and_14_out, M, pg_0_g);
  and and_15 (and_15_out, M, CI);
  or or_1 (G, and_2_out, and_3_out, and_4_out, pg_3_g);
  or or_2 (or_2_out, and_6_out, and_7_out, and_8_out, and_9_out);
  or or_3 (or_3_out, and_10_out, and_11_out, and_12_out);
  or or_4 (or_4_out, and_13_out, and_14_out);
  xor xor_1 (xor_1_out, pg_3_g, pg_3_p);
  xor xor_2 (xor_2_out, pg_2_g, pg_2_p);
  xor xor_3 (xor_3_out, pg_1_g, pg_1_p);
  xor xor_4 (xor_4_out, pg_0_g, pg_0_p);
  or or_5 (CO, and_1_out, G);
  xor xor_5 (F[3], xor_1_out, or_2_out);
  xor xor_6 (F[2], xor_2_out, or_3_out);
  xor xor_7 (F[1], xor_3_out, or_4_out);
  xor xor_8 (F[0], xor_4_out, and_15_out);
endmodule

module pg (
  input  A,
  input  B,
  input  [3:0] S,
  output G,
  output P
);

  wire not_1_out, S0_out, S1_out, S2_out, S3_out;

  not not_1 (not_1_out, B);
  and S3 (S3_out, B, S[3], A);
  and S2 (S2_out, A, S[2], not_1_out);
  and S1 (S1_out, not_1_out, S[1]);
  and S0 (S0_out, S[0], B);
  or or_1 (G, S3_out, S2_out);
  or or_2 (P, S1_out, A, S0_out);
endmodule

module amode (
  input  B0,
  input  B1,
  input  B2,
  input  B3,
  input  B4,
  input  B5,
  input  B6,
  input  B7
);

  // Probe on {B7, B6, B5, B4, B3, B2, B1, B0}

  // Notes on the sheet:
  //   000 (zp,x) 2
  //   001 zp 1
  //   010 #imm 0
  //   011 abs 2
  //   100 (zp),y 2
  //   101 zp,x 1
  //   110 abs,y 2
  //   111 abs,x 2
  //   idx, abs/zp, x/dir
endmodule
