// Logisim project 6502_sbmpost.circ as structural Verilog: 10 circuits, main circuit cpu
module cpu (
  input  R
);

  wire clock_1_out, fsm_1_aci, fsm_1_alu, fsm_1_inc, fsm_1_mlo, fsm_1_mp, fsm_1_wa, fsm_1_wl, fsm_1_wm,
       fsm_1_wo, fsm_1_wp, fsm_1_wpc, fsm_1_wx, fsm_1_wy, pc_1_co;
  wire [1:0] fsm_1_adr, fsm_1_lco, fsm_1_rx;
  wire [3:0] alu_1_p, multiplexer_9_out, P_q;
  wire [5:0] fsm_1_aop;
  wire [7:0] A_q, alu_1_f, L_q, Mem_dout, multiplexer_2_out, multiplexer_4_out, multiplexer_5_out,
       multiplexer_6_out, multiplexer_8_out, O_q, OP, X_q, Y_q;
  wire [15:0] multiplexer_1_out, pc_1_pc, PR_q;
  wire [15:8] multiplexer_7_out;

  Clock clock_1 (.out(clock_1_out));
  Register #(.width(16)) PR (.D(multiplexer_1_out), .en(1'b1), .clk(clock_1_out), .Q(PR_q), .clr(R));
  pc pc_1 (
    .D(multiplexer_1_out), .WE(fsm_1_wpc), .INC(fsm_1_inc), .CLK(clock_1_out), .R(R), .PC(pc_1_pc),
    .CO(pc_1_co));
  // Probe on OP
  RAM #(.addrWidth(16), .databus("bibus")) Mem (
    .addr(multiplexer_1_out), .we(fsm_1_wm), .oe(1'b1), .clk(clock_1_out), .din(multiplexer_4_out),
    .dout(Mem_dout));
  Multiplexer #(.select(2), .width(16), .enable("false")) multiplexer_1 (
    .in0(pc_1_pc), .in1({multiplexer_7_out, multiplexer_8_out}), .in2({multiplexer_7_out, PR_q[7:0]}),
    .in3(PR_q), .out(multiplexer_1_out), .sel(fsm_1_adr));
  // Probe on multiplexer_1_out
  fsm fsm_1 (
    .GR(OP[1:0]), .XY(OP[2]), .AB(OP[3]), .ID(OP[4]), .OPC(OP[7:5]), .P(multiplexer_9_out), .PCO(pc_1_co),
    .CLK(clock_1_out), .R(R), .wPC(fsm_1_wpc), .INC(fsm_1_inc), .PRV(fsm_1_adr[1]), .ADR(fsm_1_adr[0]),
    .wM(fsm_1_wm), .ALU(fsm_1_alu), .LCO(fsm_1_lco[0]), .MHI(fsm_1_lco[1]), .wO(fsm_1_wo), .wL(fsm_1_wl),
    .wX(fsm_1_wx), .wY(fsm_1_wy), .wA(fsm_1_wa), .rX(fsm_1_rx[0]), .rY(fsm_1_rx[1]), .MLO(fsm_1_mlo),
    .ACI(fsm_1_aci), .AOP(fsm_1_aop), .wP(fsm_1_wp), .MP(fsm_1_mp));
  Multiplexer #(.width(8), .enable("false")) multiplexer_2 (
    .in0(Mem_dout), .in1(multiplexer_4_out), .out(multiplexer_2_out), .sel(fsm_1_alu));
  Multiplexer #(.width(8), .enable("false")) multiplexer_3 (
    .in0(O_q), .in1(multiplexer_2_out), .out(OP), .sel(fsm_1_wo));
  // Probe on multiplexer_2_out
  Register O (.D(multiplexer_2_out), .en(fsm_1_wo), .clk(clock_1_out), .Q(O_q), .clr(R));
  Register L (.D(multiplexer_2_out), .en(fsm_1_wl), .clk(clock_1_out), .Q(L_q), .clr(R));
  Register X (.D(multiplexer_2_out), .en(fsm_1_wx), .clk(clock_1_out), .Q(X_q), .clr(R));
  Register Y (.D(multiplexer_2_out), .en(fsm_1_wy), .clk(clock_1_out), .Q(Y_q), .clr(R));
  Register A (.D(multiplexer_2_out), .en(fsm_1_wa), .clk(clock_1_out), .Q(A_q), .clr(R));
  Multiplexer #(.width(8), .enable("false")) multiplexer_4 (
    .in0(alu_1_f), .in1(multiplexer_6_out), .out(multiplexer_4_out), .sel(1'b1));
  Multiplexer #(.width(8), .enable("false")) multiplexer_5 (
    .in0(L_q), .in1(multiplexer_2_out), .out(multiplexer_5_out), .sel(1'b0));
  Multiplexer #(.select(2), .width(8), .enable("false")) multiplexer_6 (
    .in0({8{1'b0}}), .in1(X_q), .in2(Y_q), .in3(A_q), .out(multiplexer_6_out), .sel(fsm_1_rx));
  // Probe on multiplexer_5_out
  // Probe on multiplexer_6_out
  // Probe on fsm_1_aop
  Register #(.width(4)) P (.D(alu_1_p), .en(fsm_1_wp), .clk(clock_1_out), .Q(P_q), .clr(R));
  Multiplexer #(.select(2), .width(8), .enable("false")) multiplexer_7 (
    .in0({8{1'b0}}), .in1(alu_1_f), .in2(multiplexer_2_out), .in3(alu_1_f), .out(multiplexer_7_out),
    .sel(fsm_1_lco));
  // Probe on multiplexer_7_out
  Multiplexer #(.width(8), .enable("false")) multiplexer_8 (
    .in0(alu_1_f), .in1(multiplexer_2_out), .out(multiplexer_8_out), .sel(fsm_1_mlo));
  // Probe on multiplexer_8_out
  // Probe on alu_1_f
  alu8 alu_1 (.B(multiplexer_5_out), .A(multiplexer_6_out), .CI(fsm_1_aci), .OP(fsm_1_aop), .F(alu_1_f), .P(alu_1_p));
  // Probe on alu_1_p
  Multiplexer #(.width(4), .enable("false")) multiplexer_9 (
    .in0(P_q), .in1(alu_1_p), .out(multiplexer_9_out), .sel(fsm_1_mp));
endmodule

module pc (
  input  [15:0] D,
  input  WE,
  input  INC,
  input  CLK,
  input  R,
  output [15:0] PC,
  output CO
);

  wire adder_1_cout, and_1_out, and_2_out, and_3_out, and_4_out, not_1_out, not_2_out, not_3_out, or_1_out,
       or_2_out, or_3_out;
  wire [7:0] adder_1_out, multiplexer_1_out, multiplexer_2_out, multiplexer_3_out;

  Multiplexer #(.width(8), .enable("false")) multiplexer_1 (
    .in0(adder_1_out), .in1(D[7:0]), .out(multiplexer_1_out), .sel(WE));
  and and_1 (and_1_out, or_1_out, and_3_out);
  Multiplexer #(.width(8), .enable("false")) multiplexer_2 (
    .in0(adder_1_out), .in1(D[15:8]), .out(multiplexer_2_out), .sel(WE));
  or or_1 (or_1_out, WE, INC);
  not not_1 (not_1_out, and_3_out);
  Register L (.D(multiplexer_1_out), .en(or_2_out), .clk(CLK), .Q(PC[7:0]), .clr(R));
  or or_2 (or_2_out, and_1_out, WE);
  Register #(.width(1)) C (.D(and_2_out), .en(1'b1), .clk(CLK), .Q(CO), .clr(R));
  and and_2 (and_2_out, and_4_out, or_1_out);
  Register H (.D(multiplexer_2_out), .en(or_3_out), .clk(CLK), .Q(PC[15:8]), .clr(R));
  or or_3 (or_3_out, not_1_out, WE);
  not not_2 (not_2_out, WE);
  Multiplexer #(.width(8), .enable("false")) multiplexer_3 (
    .in0(PC[15:8]), .in1(PC[7:0]), .out(multiplexer_3_out), .sel(and_3_out));
  // Probe on multiplexer_3_out
  and and_3 (and_3_out, not_2_out, not_3_out);
  Adder adder_1 (.a(multiplexer_3_out), .b(8'h1), .out(adder_1_out), .cout(adder_1_cout));  // open: cin
  and and_4 (and_4_out, adder_1_cout, not_3_out);
  not not_3 (not_3_out, CO);
endmodule

module fsm (
  input  [1:0] GR,
  input  XY,
  input  AB,
  input  ID,
  input  [2:0] OPC,
  input  [3:0] P,
  input  PCO,
  input  CLK,
  input  R,
  output wPC,
  output INC,
  output PRV,
  output ADR,
  output wM,
  output ALU,
  output LCO,
  output MHI,
  output wO,
  output wL,
  output wX,
  output wY,
  output wA,
  output rX,
  output rY,
  output MLO,
  output ACI,
  output [5:0] AOP,
  output wP,
  output MP
);

  wire fsm_next_1_s0, fsm_next_1_sco, fsm_next_1_shi, fsm_next_1_sin, fsm_next_1_slo, fsm_next_1_sop,
       fsm_next_1_swr, fsm_next_sig_1_ci, fsm_next_sig_1_imm, fsm_next_sig_1_zp, fsm_next_sig_1_zpy;
  wire [3:0] fsm_next_sig_1_m2r;

  fsm_next_sig fsm_next_sig_1 (
    .GR(GR), .XY(XY), .AB(AB), .ID(ID), .OPC(OPC), .P_c(P[0]), .CI(fsm_next_sig_1_ci),
    .ZP(fsm_next_sig_1_zp), .ZPY(fsm_next_sig_1_zpy), .IMM(fsm_next_sig_1_imm), .M2R(fsm_next_sig_1_m2r));  // open: ACC, R2R, BR, MA2A, CP, SH, IDM
  fsm_next fsm_next_1 (
    .CI(fsm_next_sig_1_ci), .ZP(fsm_next_sig_1_zp), .ZPY(fsm_next_sig_1_zpy), .IMM(fsm_next_sig_1_imm),
    .CLK(CLK), .R(R), .S0(fsm_next_1_s0), .SOP(fsm_next_1_sop), .SLO(fsm_next_1_slo), .SIN(fsm_next_1_sin),
    .SHI(fsm_next_1_shi), .SCO(fsm_next_1_sco), .SWR(fsm_next_1_swr));
  fsm_out fsm_out_1 (
    .S0(fsm_next_1_s0), .SOP(fsm_next_1_sop), .SLO(fsm_next_1_slo), .SIN(fsm_next_1_sin),
    .SHI(fsm_next_1_shi), .SCO(fsm_next_1_sco), .SWR(fsm_next_1_swr), .GR(GR), .XY(XY), .AB(AB), .ID(ID),
    .OPC(OPC), .CI(fsm_next_sig_1_ci), .ZP(fsm_next_sig_1_zp), .ZPY(fsm_next_sig_1_zpy),
    .M2R(fsm_next_sig_1_m2r), .wPC(wPC), .INC(INC), .PRV(PRV), .ADR(ADR), .wM(wM), .ALU(ALU), .LCO(LCO),
    .MHI(MHI), .wO(wO), .wL(wL), .wX(wX), .wY(wY), .wA(wA), .rX(rX), .rY(rY), .MLO(MLO), .ACI(ACI),
    .AOP(AOP), .wP(wP), .MP(MP));
endmodule

module fsm_next_sig (
  input  [1:0] GR,
  input  XY,
  input  AB,
  input  ID,
  input  [2:0] OPC,
  input  P_c,
  output CI,
  output ZP,
  output ZPY,
  output IMM,
  output ACC,
  output [3:0] M2R,
  output [3:0] R2R,
  output BR,
  output MA2A,
  output CP,
  output SH,
  output IDM
);

  wire and_1_out, and_2_out, and_5_out, and_9_out, and_10_out, and_12_out, and_13_out, decoder_1_out0,
       decoder_1_out2, decoder_1_out4, decoder_1_out6, decoder_1_out8, decoder_1_out9, decoder_1_out10,
       decoder_1_out11, decoder_1_out12, decoder_1_out13, decoder_1_out14, decoder_1_out15, decoder_2_out0,
       decoder_2_out4, decoder_2_out6, decoder_2_out8, decoder_2_out12, decoder_2_out14, not_2_out,
       not_3_out, not_4_out, not_5_out, not_6_out, not_7_out, not_8_out, or_1_out, or_2_out, or_3_out,
       or_4_out, or_5_out, or_6_out, or_7_out, or_8_out, or_9_out, or_10_out, or_11_out, or_12_out,
       or_13_out, or_16_out, xor_1_out;
  wire [1:0] not_1_out;

  assign not_1_out = ~GR;  // NOT_Gate not_1, 2 bits wide
  Decoder #(.select(4), .enable("false")) decoder_1 (
    .out0(decoder_1_out0), .out2(decoder_1_out2), .out4(decoder_1_out4), .out6(decoder_1_out6),
    .out8(decoder_1_out8), .out9(decoder_1_out9), .out10(decoder_1_out10), .out11(decoder_1_out11),
    .out12(decoder_1_out12), .out13(decoder_1_out13), .out14(decoder_1_out14), .out15(decoder_1_out15),
    .sel({OPC, ID}));  // open: out1, out3, out5, out7
  Decoder #(.select(4), .enable("false")) decoder_2 (
    .out0(decoder_2_out0), .out4(decoder_2_out4), .out6(decoder_2_out6), .out8(decoder_2_out8),
    .out12(decoder_2_out12), .out14(decoder_2_out14), .sel({AB, XY, GR}));  // open: out1, out2, out3, out5, out7, out9, out10, out11, out13, out15
  not not_2 (not_2_out, XY);
  not not_3 (not_3_out, AB);
  and and_1 (and_1_out, not_1_out[1], GR[0]);
  and and_2 (and_2_out, not_1_out[0], GR[1]);
  or or_1 (or_1_out, decoder_1_out13, decoder_1_out12);
  or or_2 (or_2_out, decoder_1_out12, decoder_1_out14);
  xor xor_1 (xor_1_out, not_3_out, and_1_out);
  not not_4 (not_4_out, ID);
  or or_3 (or_3_out, decoder_1_out0, decoder_1_out4);
  or or_4 (or_4_out, decoder_1_out2, decoder_1_out6);
  or or_5 (or_5_out, decoder_1_out10, decoder_1_out11);
  or or_6 (or_6_out, decoder_1_out8, decoder_1_out9);
  or or_7 (or_7_out, decoder_1_out8, decoder_1_out9, decoder_1_out10, decoder_1_out11);
  or or_8 (or_8_out, decoder_1_out10, decoder_1_out9);
  or or_9 (or_9_out, decoder_1_out12, decoder_1_out14);
  or or_10 (or_10_out, decoder_2_out0, decoder_2_out4, decoder_2_out12);
  or or_11 (or_11_out, decoder_2_out6, decoder_2_out14);
  or or_12 (or_12_out, or_1_out, or_2_out, decoder_1_out15);
  not not_5 (not_5_out, decoder_2_out8);
  not not_6 (not_6_out, decoder_2_out12);
  and and_3 (M2R[0], or_3_out, decoder_2_out8);
  and and_4 (M2R[1], or_4_out, decoder_2_out8);
  and and_5 (and_5_out, not_5_out, not_6_out);
  and and_6 (R2R[0], or_7_out, decoder_2_out12);
  not not_7 (not_7_out, BR);
  and and_7 (R2R[1], or_8_out, decoder_2_out8);
  and and_8 (R2R[2], or_9_out, decoder_2_out8);
  and and_9 (and_9_out, decoder_1_out8, decoder_2_out8);
  and and_10 (and_10_out, decoder_1_out12, decoder_2_out12);
  and and_11 (BR, ID, decoder_2_out0);
  and and_12 (and_12_out, GR[0], or_1_out);
  and and_13 (and_13_out, or_2_out, or_10_out);
  not not_8 (not_8_out, ID);
  or or_13 (or_13_out, decoder_2_out12, or_11_out);
  and and_14 (IDM, or_11_out, or_12_out);
  and and_15 (M2R[2], or_5_out, and_5_out, not_7_out);
  and and_16 (M2R[3], and_5_out, or_6_out, not_7_out);
  or or_14 (R2R[3], and_9_out, and_10_out);
  or or_15 (CP, and_12_out, and_13_out);
  and and_17 (SH, not_8_out, or_13_out);
  or or_16 (or_16_out, ZPY, AB);
  and and_18 (CI, or_16_out, P_c);
  and and_19 (ZP, not_4_out, not_3_out, XY);
  and and_20 (ZPY, ID, not_3_out, not_2_out);
  and and_21 (IMM, not_4_out, not_2_out, xor_1_out);
  and and_22 (ACC, not_4_out, AB, not_2_out, and_2_out);

  assign MA2A = GR[0];

  // Notes on the sheet:
  //   HI
  //   LO
  //   PH
  //   PL
  //   LD
  //   ST
  //   TRX
  //   TRY
  //   IXY
  //   DXY
  //   BR
  //   TODO: NO LD, ST, CP
  //   SH
endmodule

module fsm_next (
  input  CI,
  input  ZP,
  input  ZPY,
  input  IMM,
  input  CLK,
  input  R,
  output S0,
  output SOP,
  output SLO,
  output SIN,
  output SHI,
  output SCO,
  output SWR
);

  wire and_3_out, and_5_out, and_6_out, and_7_out, not_1_out, not_2_out, not_3_out, not_4_out, not_5_out,
       not_6_out, not_7_out, not_8_out, not_9_out, not_10_out;
  wire [5:0] or_3_out;

  not not_1 (not_1_out, IMM);
  not not_2 (not_2_out, ZPY);
  not not_3 (not_3_out, ZP);
  not not_4 (not_4_out, CI);
  and and_1 (or_3_out[1], SOP, not_1_out);
  and and_2 (or_3_out[2], SLO, ZPY);
  and and_3 (and_3_out, SLO, not_2_out, not_3_out);
  and and_4 (or_3_out[4], SHI, CI);
  and and_5 (and_5_out, SHI, not_4_out);
  and and_6 (and_6_out, SLO, ZP);
  and and_7 (and_7_out, SOP, IMM);
  or or_1 (or_3_out[3], SIN, and_3_out);
  or or_2 (or_3_out[5], SCO, and_5_out, and_6_out, and_7_out);
  and and_8 (S0, not_5_out, not_6_out, not_7_out, not_8_out, not_9_out, not_10_out);
  or or_3 (or_3_out[0], S0, SWR);
  Register #(.width(6)) register_1 (.D(or_3_out), .en(1'b1), .clk(CLK), .Q({SWR, SCO, SHI, SIN, SLO, SOP}), .clr(R));
  not not_5 (not_5_out, SOP);
  not not_6 (not_6_out, SLO);
  not not_7 (not_7_out, SIN);
  not not_8 (not_8_out, SHI);
  not not_9 (not_9_out, SCO);
  not not_10 (not_10_out, SWR);
endmodule

module fsm_out (
  input  S0,
  input  SOP,
  input  SLO,
  input  SIN,
  input  SHI,
  input  SCO,
  input  SWR,
  input  [1:0] GR,
  input  XY,
  input  AB,
  input  ID,
  input  [2:0] OPC,
  input  CI,
  input  ZP,
  input  ZPY,
  input  [3:0] M2R,
  output wPC,
  output INC,
  output PRV,
  output ADR,
  output wM,
  output ALU,
  output LCO,
  output MHI,
  output wO,
  output wL,
  output wX,
  output wY,
  output wA,
  output rX,
  output rY,
  output MLO,
  output ACI,
  output [5:0] AOP,
  output wP,
  output MP
);

  wire and_1_out, and_2_out, and_4_out, not_2_out, not_3_out, not_4_out, or_1_out, or_2_out;
  wire [1:0] not_1_out;

  assign not_1_out = ~GR;  // NOT_Gate not_1, 2 bits wide
  not not_2 (not_2_out, SIN);
  not not_3 (not_3_out, SCO);
  or or_1 (or_1_out, ZP, ZPY);
  and and_1 (and_1_out, SWR, M2R[2]);
  and and_2 (and_2_out, not_2_out, not_3_out);
  and and_3 (MLO, SLO, or_1_out);
  and and_4 (and_4_out, SHI, AB);
  or or_2 (or_2_out, AB, ZPY);
  not not_4 (not_4_out, XY);
  or or_3 (INC, S0, and_4_out, SOP, SWR);
  or or_4 (ADR, SHI, SIN, MLO);
  and and_5 (MHI, SHI, or_2_out);
  or or_5 (wL, SIN, SHI, SLO);
  and and_6 (wX, and_1_out, not_1_out[0], GR[1]);
  and and_7 (wY, not_1_out[0], not_1_out[1], and_1_out);
  and and_8 (wA, and_1_out, not_1_out[1], GR[0]);
  and and_9 (rX, XY, ID, and_2_out);
  and and_10 (rY, and_2_out, ID, not_4_out);
  or or_6 (ACI, SIN, SCO);

  assign ALU = 1'b0;
  assign AOP = 6'b011001;
  assign LCO = SCO;
  assign MP = SHI;
  assign PRV = SCO;
  assign wM = 1'b0;
  assign wO = SOP;
  assign wP = SWR;
  assign wPC = 1'b0;
endmodule

module alu8 (
  input  [7:0] B,
  input  [7:0] A,
  input  CI,
  input  [5:0] OP,
  output [7:0] F,
  output [3:0] P
);

  wire and_1_out, hi_co, lo_g, lo_p, or_1_out;
  wire [3:0] hi_f, lo_f;

  // Probe on OP
  or or_1 (or_1_out, lo_g, and_1_out);
  alu4 lo (.B(B[3:0]), .A(A[3:0]), .CI(CI), .S(OP[3:0]), .M(OP[4]), .G(lo_g), .P(lo_p), .F(lo_f));  // open: CO
  and and_1 (and_1_out, lo_p, CI);
  alu4 hi (.B(B[7:4]), .A(A[7:4]), .CI(or_1_out), .S(OP[3:0]), .M(OP[4]), .CO(hi_co), .F(hi_f));  // open: G, P
  Multiplexer #(.width(8), .enable("false")) multiplexer_1 (
    .in0({hi_f, lo_f}), .in1({CI, A[7:1]}), .out(F), .sel(OP[5]));
  Multiplexer #(.enable("false")) multiplexer_2 (.in0(hi_co), .in1(A[0]), .out(P[0]), .sel(OP[5]));

  assign P[3:1] = 3'b000;

  // Notes on the sheet:
  //   s,m,s3-s0
endmodule

module alu4 (
  input  [3:0] B,
  input  [3:0] A,
  input  CI,
  input  [3:0] S,
  input  M,
  output CO,
  output G,
  output P,
  output [3:0] F
);

  wire and_1_out, and_2_out, and_3_out, and_4_out, and_6_out, and_7_out, and_8_out, and_9_out, and_10_out,
       and_11_out, and_12_out, and_13_out, and_14_out, and_15_out, or_2_out, or_3_out, or_4_out, pg_0_g,
       pg_0_p, pg_1_g, pg_1_p, pg_2_g, pg_2_p, pg_3_g, pg_3_p, xor_1_out, xor_2_out, xor_3_out, xor_4_out;

  pg pg_3 (.A(A[3]), .B(B[3]), .S(S), .G(pg_3_g), .P(pg_3_p));
  pg pg_2 (.A(A[2]), .B(B[2]), .S(S), .G(pg_2_g), .P(pg_2_p));
  pg pg_1 (.A(A[1]), .B(B[1]), .S(S), .G(pg_1_g), .P(pg_1_p));
  pg pg_0 (.A(A[0]), .B(B[0]), .S(S), .G(pg_0_g), .P(pg_0_p));
  and and_1 (and_1_out, CI, pg_0_p, pg_1_p, pg_2_p, pg_3_p);
  and and_2 (and_2_out, pg_0_g, pg_1_p, pg_2_p, pg_3_p);
  and and_3 (and_3_out, pg_1_g, pg_2_p, pg_3_p);
  and and_4 (and_4_out, pg_2_g, pg_3_p);
  and and_5 (P, pg_0_p, pg_1_p, pg_2_p, pg_3_p);
  and and_6 (and_6_out, M, CI, pg_0_p, pg_1_p, pg_2_p);
  and and_7 (and_7_out, M, pg_0_g, pg_1_p, pg_2_p);
  and and_8 (and_8_out, M, pg_1_g, pg_2_p);
  and and_9 (and_9_out, M, pg_2_g);
  and and_10 (and_10_out, M, CI, pg_1_p, pg_0_p);
  and and_11 (and_11_out, M, pg_0_g, pg_1_p);
  and and_12 (and_12_out, M, pg_1_g);
  and and_13 (and_13_out, M, CI, pg_0_p);
  and and_14 (and_14_out, M, pg_0_g);
  and and_15 (and_15_out, M, CI);
  or or_1 (G, and_2_out, and_3_out, and_4_out, pg_3_g);
  or or_2 (or_2_out, and_6_out, and_7_out, and_8_out, and_9_out);
  or or_3 (or_3_out, and_10_out, and_11_out, and_12_out);
  or or_4 (or_4_out, and_13_out, and_14_out);
  xor xor_1 (xor_1_out, pg_3_g, pg_3_p);
  xor xor_2 (xor_2_out, pg_2_g, pg_2_p);
  xor xor_3 (xor_3_out, pg_1_g, pg_1_p);
  xor xor_4 (xor_4_out, pg_0_g, pg_0_p);
  or or_5 (CO, and_1_out, G);
  xor xor_5 (F[3], xor_1_out, or_2_out);
  xor xor_6 (F[2], xor_2_out, or_3_out);
  xor xor_7 (F[1], xor_3_out, or_4_out);
  xor xor_8 (F[0], xor_4_out, and_15_out);
endmodule

module pg (
  input  A,
  input  B,
  input  [3:0] S,
  output G,
  output P
);

  wire not_1_out, S0_out, S1_out, S2_out, S3_out;

  not not_1 (not_1_out, B);
  and S3 (S3_out, B, S[3], A);
  and S2 (S2_out, A, S[2], not_1_out);
  and S1 (S1_out, not_1_out, S[1]);
  and S0 (S0_out, S[0], B);
  or or_1 (G, S3_out, S2_out);
  or or_2 (P, S1_out, A, S0_out);
endmodule

module amode (
  input  B0,
  input  B1,
  input  B2,
  input  B3,
  input  B4,
  input  B5,
  input  B6,
  input  B7
);

  // Probe on {B7, B6, B5, B4, B3, B2, B1, B0}

  // Notes on the sheet:
  //   000 (zp,x) 2
  //   001 zp 1
  //   010 #imm 0
  //   011 abs 2
  //   100 (zp),y 2
  //   101 zp,x 1
  //   110 abs,y 2
  //   111 abs,x 2
  //   idx, abs/zp, x/dir
endmodule
